# Fritzing sketch Tree.0_PressureSensor (saved by Fritzing 0.9.3b)
breadboards: 1

parts:
  Part1 = Arduino Board Ethernet
  J1 = Basic Force Sensing Resistor (FSR) [package=THT]
  J2 = Basic Force Sensing Resistor (FSR) [package=THT]
  J3 = Basic Force Sensing Resistor (FSR) [package=THT]
  J4 = Basic Force Sensing Resistor (FSR) [package=THT]
  R1 = Resistor [tolerance=±5% resistance=220 package=THT]
  R2 = Resistor [tolerance=±5% resistance=220 package=THT]
  R3 = Resistor [tolerance=±5% resistance=220 package=THT]
  R4 = Resistor [tolerance=±5% resistance=220 package=THT]

nets:
  N1: Part1.A0, J1.pin_0, R4.Pin_1
  N2: Part1.A1, J2.pin_0, R3.Pin_1
  N3: Part1.A2, J3.pin_0, R2.Pin_1
  N4: Part1.A3, J4.pin_0, R1.Pin_1
  5V: Part1.5V, R1.Pin_0, R2.Pin_0, R3.Pin_0, R4.Pin_0
  GND: Part1.GND, J1.pin_1, J2.pin_1, J3.pin_1, J4.pin_1

notes:
  Leonardo ETH with PoE
  from Arduino.org
  NOT Arduino.cc
